// Logisim project control_logic.circ as structural Verilog: 3 circuits, main circuit control_logic
module control_logic (
  input  [31:0] inst,
  input  BrEq,
  input  BrLt,
  output PCSel,
  output RegWEn,
  output [2:0] ImmSel,
  output BrUn,
  output ASel,
  output BSel,
  output [3:0] ALUSel,
  output MemRW,
  output [1:0] WBSel,
  output CSRSel,
  output CSRWen
);

  I_Type_Decode i_type_decode_1 (.Instruction(inst), .ALUSel(ALUSel), .RegWEn(RegWEn));

  // Notes on the sheet:
  //   INPUTS to your circuit
  //   DON'T CHANGE THE LOCATIONS OF THE INPUTS AND OUTPUTS!
  //   OUTPUT from your circuit
endmodule

module ALU_Decode (
  input  [2:0] funct3,
  input  srl_sra,
  output [3:0] ALUSel
);

  wire [3:0] sra_l_0;

  Multiplexer #(.enable("false"), .select(3), .width(4)) multiplexer_1 (
    .in0(4'b0000), .in1(4'b0110), .in2(4'b0111), .in3(4'b0111), .in4(4'b0011), .in5(sra_l_0), .in6(4'b0010),
    .in7(4'b0001), .out(ALUSel), .sel(funct3));
  Multiplexer #(.enable("false"), .width(4)) multiplexer_2 (.in0(4'b0100), .in1(4'b0101), .out(sra_l_0), .sel(srl_sra));
endmodule

module I_Type_Decode (
  input  [31:0] Instruction,
  output [3:0] ALUSel,
  output RegWEn
);

  ALU_Decode alu_decode_1 (.funct3(Instruction[14:12]), .srl_sra(Instruction[30]), .ALUSel(ALUSel));

  assign RegWEn = 1'b1;
endmodule
